# Fritzing sketch guvenlik_sistemi (saved by Fritzing 0.9.3b)
breadboards: 1

parts:
  Keypad4x1 = Keypad Membran 4x4
  Raspberry_Pi_1 = Raspberry Pi 3 [part_number=RPI-3-V1.2]
  R1 = Resistor [tolerance=±5% resistance=220 package=THT]
  LED1 = LED - 5mm [color="Red (633nm)" package="5 mm [THT]"]
  S1 = SPST Switch [package=switch-spdt-smd]
  J1 = Piezo Speaker
  Part1 = HC-SR501 Body Sensor Module

nets:
  N1: Keypad4x1.Pin1, Raspberry_Pi_1.GIPO4
  N2: Keypad4x1.Pin2, Raspberry_Pi_1.GIPO14
  N3: Keypad4x1.Pin3, Raspberry_Pi_1.GIPO15
  N4: Keypad4x1.Pin4, Raspberry_Pi_1.GIPO17
  N5: Keypad4x1.Pin5, Raspberry_Pi_1.GIPO18
  N6: Keypad4x1.Pin6, Raspberry_Pi_1.GIPO27
  N7: Keypad4x1.Pin7, Raspberry_Pi_1.GIPO22
  N8: Keypad4x1.Pin8, Raspberry_Pi_1.GIPO23
  GND: Raspberry_Pi_1.GND, R1.Pin_1, S1.P, J1.pin1, Part1.GND
  N9: Raspberry_Pi_1.GIPO26, S1.S
  N10: Raspberry_Pi_1.GIPO20, J1.pin2
  N11: Raspberry_Pi_1.GIPO25, Part1.OUT
  N12: Raspberry_Pi_1.GIPO24, LED1.anode
  5V: Raspberry_Pi_1.5V, S1.O, Part1.VCC
  N13: R1.Pin_0, LED1.cathode

custom parts:
  Keypad Membran 4x4: Membrane Keypad 4x4 Matrix
  HC-SR501 Body Sensor Module: Pyroelectric Infrared PIR Motion Sensor Detector Module
